# Fritzing sketch Echidnashield (saved by Fritzing 0.9.2b)
breadboards: 1

parts:
  Parte1 = Arduino Uno (Rev3)
  PINES_MODO_MAKEY = female pin header, 9 pins [form="♀ (female)"]
  S1 = Toggle Switch [package=THT]
  R1 = Resistor [tolerance=±5% resistance=22m package=THT]
  D1 = Schottky Diode [part_number=1N5817 package="300 mil [THT]"]
  R2 = Resistor [tolerance=±5% resistance=22m package=THT]
  D2 = Schottky Diode [part_number=1N5817 package="300 mil [THT]"]
  R3 = Resistor [tolerance=±5% resistance=22m package=THT]
  D3 = Schottky Diode [part_number=1N5817 package="300 mil [THT]"]
  R4 = Resistor [tolerance=±5% resistance=22m package=THT]
  D4 = Schottky Diode [part_number=1N5817 package="300 mil [THT]"]
  R5 = Resistor [tolerance=±5% resistance=22m package=THT]
  D5 = Schottky Diode [part_number=1N5817 package="300 mil [THT]"]
  R6 = Resistor [tolerance=±5% resistance=22m package=THT]
  D6 = Schottky Diode [part_number=1N5817 package="300 mil [THT]"]
  R7 = Resistor [tolerance=±5% resistance=22m package=THT]
  D7 = Schottky Diode [part_number=1N5817 package="300 mil [THT]"]
  D8 = Schottky Diode [part_number=1N5817 package="300 mil [THT]"]
  LED1 = smd LED [color="Red (633nm)" package="0603 [SMD]"]
  R8 = Resistor [tolerance=±5% resistance=22m package=THT]
  R9 = Resistor [tolerance=±5% resistance=220 package=THT]
  LED2 = smd LED [color="Orange (620nm)" package="0603 [SMD]"]
  R10 = Resistor [tolerance=±5% resistance=220 package=THT]
  LED3 = smd LED [color="Green (560nm)" package="0603 [SMD]"]
  R11 = Resistor [tolerance=±5% resistance=220 package=THT]
  LED4 = RGB LED (com. cathode, rbg) [package="5 mm [THT]"]
  R12 = Resistor [tolerance=±5% resistance=220 package=THT]
  Q1 = TRANSISTOR_NPN [package=to-92]
  SG1 = Buzzer 12mm [package=buzzer-12mm]
  R13 = Resistor [tolerance=±5% resistance=10k package=THT]
  SERVO_1 = female pin header, 3 pins [form="♀ (female)"]
  SERVO_2 = female pin header, 3 pins [form="♀ (female)"]
  SERVO_3 = female pin header, 3 pins [form="♀ (female)"]
  R14 = Photocell (LDR) [package=THT]
  R15 = Resistor [tolerance=±5% resistance=10k package=THT]
  D9 = Schottky Diode [part_number=1N5817 package="300 mil [THT]"]
  D10 = Schottky Diode [part_number=1N5817 package="300 mil [THT]"]
  D11 = Schottky Diode [part_number=1N5817 package="300 mil [THT]"]
  D12 = Schottky Diode [part_number=1N5817 package="300 mil [THT]"]
  D13 = Schottky Diode [part_number=1N5817 package="300 mil [THT]"]
  D14 = Schottky Diode [part_number=1N5817 package="300 mil [THT]"]
  D15 = Schottky Diode [part_number=1N5817 package="300 mil [THT]"]
  D16 = Schottky Diode [part_number=1N5817 package="300 mil [THT]"]
  S3 = SWITCH-MOMENTARY-2 [package=tactile-pth-12mm]
  S2 = SWITCH-MOMENTARY-2 [package=tactile-pth-12mm]
  R17 = Resistor [tolerance=±5% resistance=10k package=THT]
  R16 = Resistor [tolerance=±5% resistance=10k package=THT]
  U1 = Thumb Joystick [package=joystick]
  J1 = Infrared Proximity Sensor
  C1 = Ceramic Capacitor [capacitance=0.1µF package="100 mil [THT, multilayer]"]
  R18 = Resistor [tolerance=±5% resistance=10k package=THT]
  U2 = MMA7361 [package=lga14]
  C2 = Ceramic Capacitor [capacitance=100nF package="100 mil [THT, multilayer]"]
  C3 = Ceramic Capacitor [capacitance=100nF package="100 mil [THT, multilayer]"]

nets:
  N1: Parte1.A0, PINES_MODO_MAKEY.pin6, D6.cathode, D14.cathode
  N2: Parte1.A1, PINES_MODO_MAKEY.pin5, D3.cathode, D11.cathode
  N3: Parte1.A2, PINES_MODO_MAKEY.pin4, D5.cathode, D13.cathode
  N4: Parte1.A3, PINES_MODO_MAKEY.pin3, D4.cathode, D12.cathode
  N5: Parte1.A5/SCL, PINES_MODO_MAKEY.pin1, D1.cathode, D9.cathode
  N6: Parte1.D8, SERVO_3.pin1
  N7: Parte1.D9_PWM, LED4.green_anode
  N8: Parte1.D10_PWM/SS, R13.Pin_1
  N9: Parte1.D11_PWM/MOSI, R11.Pin_1
  N10: Parte1.D12/MISO, R10.Pin_1
  N11: Parte1.D13/SCK, R9.Pin_1
  N12: Parte1.GND, R1.Pin_0, R2.Pin_0, R3.Pin_0, R4.Pin_0, R5.Pin_0, R6.Pin_0, R7.Pin_0, LED1.cathode, R8.Pin_0, LED2.cathode, LED3.cathode, R12.Pin_0, Q1.E, SERVO_1.pin3, SERVO_2.pin3, SERVO_3.pin3, R15.Pin_0, R17.Pin_1, R16.Pin_1, U1.H-, U1.V-
  N13: Parte1.A4/SDA, PINES_MODO_MAKEY.pin2, D2.cathode, D10.cathode
  N14: Parte1.D2, PINES_MODO_MAKEY.pin7, D7.cathode, D16.cathode
  N15: Parte1.D3_PWM, PINES_MODO_MAKEY.pin8, D8.cathode, D15.cathode
  N16: Parte1.D4, SERVO_1.pin1
  N17: Parte1.D5_PWM, LED4.red_anode
  N18: Parte1.D6_PWM, LED4.blue_anode
  N19: Parte1.D7, SERVO_2.pin1
  N20: Parte1.5V, S1.COM, SG1.1, SERVO_1.pin2, SERVO_2.pin2, SERVO_3.pin2
  N21: PINES_MODO_MAKEY.pin9, S1.L1
  VCC: S1.L2, R14.pin_1, S3.1, S2.1, U1.V+, U1.H+, J1.Vcc, C1.1, R18.Pin_1, U2.VDD
  N22: R1.Pin_1, D1.anode
  N23: R2.Pin_1, D2.anode
  N24: R3.Pin_1, D3.anode
  N25: R4.Pin_1, D4.anode
  N26: R5.Pin_1, D5.anode
  N27: R6.Pin_1, D6.anode
  N28: R7.Pin_1, D7.anode
  N29: D8.anode, R8.Pin_1
  N30: LED1.anode, R9.Pin_0
  N31: LED2.anode, R10.Pin_0
  N32: LED3.anode, R11.Pin_0
  N33: LED4.common_cathode, R12.Pin_1
  N34: Q1.B, R13.Pin_0
  N35: Q1.C, SG1.2
  N36: R14.pin_0, R15.Pin_1, D14.anode
  N37: D9.anode, U2.XOUT, C2.1
  N38: D10.anode, U2.YOUT, C3.1
  N39: D11.anode, J1.Vout
  N40: D12.anode, U1.V
  N41: D13.anode, U1.H
  N42: D15.anode, S3.2, R17.Pin_0
  N43: D16.anode, S2.2, R16.Pin_0
  GND: J1.GND, C1.0, U2.VSS, C2.0, C3.0
  N44: R18.Pin_0, U2.SLEEP
